# Fritzing sketch motor_test (saved by Fritzing 1.0.2b)
breadboards: 1

parts:
  Mod1 = Raspberry Pi Pico W
  M1 = gear-motor
  L298N1 = L298N DC motor driver
  VCC1 = Battery block 9V

nets:
  N1: Mod1.pin_3, Mod1.pin_8, Mod1.pin_13, Mod1.pin_18, Mod1.pin_23, Mod1.pin_28, Mod1.pin_33, Mod1.pin_38, L298N1.5V#9
  N2: Mod1.pin_4, L298N1.ENA
  N3: Mod1.pin_5, L298N1.IN1
  N4: Mod1.pin_6, L298N1.IN2
  N5: Mod1.pin_39, L298N1.5V#10
  N6: M1.pin_1, L298N1.OUT2
  N7: M1.pin_2, L298N1.OUT1
  N8: L298N1.12V, VCC1.+
  N9: L298N1.GND, VCC1.-

custom parts:
  Raspberry Pi Pico W: Raspberry Pi Pico W. Based around the RP2040 microcontroller the Pico W is a low cost microcontroller device bringing Raspberry Pi quality, cost, and easy of use to the microcontroller space. The areas marked KEEPOUT in pcb silkscreen should not have traces running through them to avoid shorts on a soldered in module!
  L298N DC motor driver: 2x DC motor driver with 78M05 positive voltage regulator (7..35 V) L298N: max 46 V, 2 A Set 5 V Enable jumper to enable 5 V regultor (needed for the L298N) and +5 V output at screw terminal or supply external +5 V at screw terminal Set ENA and/or ENB to +5 V to enable motor permanently or supply ENA and/or ENB with PWM signal IN1 and IN2 set rotation directory for motor A (OUT1/OUT2) IN2 and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
